# Fritzing sketch hc-sr501_IR_movement_detection_sensor (saved by Fritzing 0.9.3b)

parts:
  U1 = NodeMCU V3.0
  Part1 = HC-SR501 Body Sensor Module

nets:
  N1: U1.D0, Part1.OUT
  N2: U1.VU, Part1.VCC
  GND: U1.GND, Part1.GND

custom parts:
  NodeMCU V3.0: ESP8266 based NodeMCU
  HC-SR501 Body Sensor Module: Pyroelectric Infrared PIR Motion Sensor Detector Module
