# Fritzing sketch lm35_temperature_sensor (saved by Fritzing 0.9.3b)

parts:
  U1 = NodeMCU V3.0
  T1 = LM35 Temperature Sensor [package="TO92 [THT]"]

nets:
  N1: U1.VU, T1.+Vs
  GND: U1.GND, T1.GND
  N2: U1.A0, T1.Vout

custom parts:
  NodeMCU V3.0: ESP8266 based NodeMCU
