# Fritzing sketch oled (saved by Fritzing 0.9.3b)

parts:
  U1 = NodeMCU V3.0
  Squix1 = OLED 0.96" 128x64 I2C SSD1306

nets:
  N1: U1.D1, Squix1.SCL
  N2: U1.D2, Squix1.SCA
  3V3: U1.3V3, Squix1.VCC
  GND: U1.GND, Squix1.GND

custom parts:
  NodeMCU V3.0: ESP8266 based NodeMCU
